// Logisim project lastname_firstname.circ as structural Verilog
module main (
);

  wire clk, comparator_1_eq, DBUF_COND, DBUF_selMEM, DBUF_WB, DBUF_WtMEM, EBUF_selMEM, EBUF_WB, EBUF_WtMEM,
       ID_BR, ID_JMP, ID_selB, ID_selREG, MBUF_WB, or_1_out;
  wire [1:0] DBUF_func, FORWARD_A, FORWARD_B;
  wire [3:0] DBUF_Rx, EBUF_Rx, MBUF_Rx, multiplexer_4_out;
  wire [19:0] FBUF_IMM;
  wire [31:0] adder_1_out, adder_2_out, DBUF_A, DBUF_B, DBUF_RESULT, dual_ported_register_file_1_out2,
       EBUF_B, EBUF_RESULT, EX_RESULT, FBUF_PC, ID_B, ID_IMM, MBUF_RESULT, multiplexer_3_out, PC_q,
       ram_1_data, ram_2_data;
  wire [31:20] FBUF_IR;

  Clock clock_1 (.out(clk));
  Register #(.width(32)) PC (.D(multiplexer_3_out), .Q(PC_q), .clk(clk));  // open: en, clr
  Multiplexer #(.select(2), .width(32)) multiplexer_1 (
    .in0(ID_B), .in1(EX_RESULT), .in2(EX_RESULT), .in3(MBUF_RESULT), .out(DBUF_B), .sel(FORWARD_B));  // open: en
  Adder #(.width(32)) adder_1 (.a(32'h1), .b(PC_q), .out(adder_1_out));  // open: cin, cout
  Multiplexer #(.select(2), .width(32)) multiplexer_2 (
    .in0(EX_RESULT), .in1(EX_RESULT), .in2(EX_RESULT), .in3(MBUF_RESULT), .out(DBUF_A), .sel(FORWARD_A));  // open: en
  Multiplexer #(.width(32)) multiplexer_3 (
    .in0(adder_1_out), .in1(DBUF_RESULT), .out(multiplexer_3_out), .sel(DBUF_COND));  // open: en
  assign ID_IMM = {{12{FBUF_IMM[19]}}, FBUF_IMM};  // Bit_Extender bit_extender_1
  Multiplexer #(.width(4)) multiplexer_4 (
    .in0(FBUF_IR[27:24]), .in1(FBUF_IMM[3:0]), .out(multiplexer_4_out), .sel(ID_selREG));  // open: en
  Comparator #(.width(32)) comparator_1 (.a(DBUF_A), .b(DBUF_B), .eq(comparator_1_eq));  // open: gt, lt
  RAM #(.addrWidth(24), .dataWidth(32)) ram_1 (
    .addr(PC_q[23:0]), .data(ram_1_data), .clk(clk), .ld(1'b1));  // open: sel, clr
  Adder #(.width(32)) adder_2 (.a(ID_IMM), .b(FBUF_PC), .out(adder_2_out));  // open: cin, cout
  or or_1 (or_1_out, comparator_1_eq, ID_BR);
  ALU alu_1 (.A(DBUF_A), .B(DBUF_B), .func(DBUF_func), .ALUout(EX_RESULT));
  Register #(.width(32)) register_1 (.D(adder_1_out), .en(1'b1), .Q(FBUF_PC), .clk(clk));  // open: clr
  Register #(.width(32)) register_2 (.D(ram_1_data), .en(1'b1), .Q({FBUF_IR, FBUF_IMM}), .clk(clk));  // open: clr
  Multiplexer #(.width(32)) multiplexer_5 (
    .in0(adder_2_out), .in1(EX_RESULT), .out(DBUF_RESULT), .sel(ID_JMP));  // open: en
  Register #(.width(32)) register_3 (.D(DBUF_A), .en(1'b1), .Q(DBUF_A), .clk(clk));  // open: clr
  or or_2 (DBUF_COND, or_1_out, ID_JMP);
  Register #(.width(32)) register_4 (.D(DBUF_B), .en(1'b1), .Q(DBUF_B), .clk(clk));  // open: clr
  RAM #(.addrWidth(24), .dataWidth(32), .bus("separate")) ram_2 (
    .addr(EBUF_RESULT[23:0]), .din(EBUF_B), .data(ram_2_data), .str(EBUF_WtMEM), .clk(clk), .ld(1'b1));  // open: sel, clr
  Register #(.width(32)) register_5 (.D(DBUF_RESULT), .en(1'b1), .Q(DBUF_RESULT), .clk(clk));  // open: clr
  Dual_Ported_Register_File dual_ported_register_file_1 (
    .CLK(clk), .WrREGNO(MBUF_Rx), .RdREGNO1(FBUF_IR[23:20]), .RdREGNO2(multiplexer_4_out),
    .INPUT(MBUF_RESULT), .OUT1(EX_RESULT), .OUT2(dual_ported_register_file_1_out2), .WrEN(MBUF_WB));
  Multiplexer #(.width(32)) multiplexer_6 (
    .in0(ram_2_data), .in1(EBUF_RESULT), .out(EX_RESULT), .sel(EBUF_selMEM));  // open: en
  Register #(.width(1)) register_6 (.D(DBUF_COND), .en(1'b1), .Q(DBUF_COND), .clk(clk));  // open: clr
  Register #(.width(32)) register_7 (.D(EX_RESULT), .en(1'b1), .Q(EBUF_RESULT), .clk(clk));  // open: clr
  Register #(.width(1)) register_8 (.D(DBUF_WtMEM), .en(1'b1), .Q(EBUF_WtMEM), .clk(clk));  // open: clr
  Register #(.width(32)) register_9 (.D(DBUF_B), .en(1'b1), .Q(EBUF_B), .clk(clk));  // open: clr
  Register #(.width(4)) register_10 (.D(DBUF_Rx), .en(1'b1), .Q(EBUF_Rx), .clk(clk));  // open: clr
  Register #(.width(1)) register_11 (.D(DBUF_WB), .en(1'b1), .Q(EBUF_WB), .clk(clk));  // open: clr
  Register #(.width(1)) register_12 (.D(DBUF_selMEM), .en(1'b1), .Q(EBUF_selMEM), .clk(clk));  // open: clr
  Multiplexer #(.width(32)) multiplexer_7 (
    .in0(dual_ported_register_file_1_out2), .in1(ID_IMM), .out(ID_B), .sel(ID_selB));  // open: en
  Register #(.width(32)) register_13 (.D(EX_RESULT), .en(1'b1), .Q(MBUF_RESULT), .clk(clk));  // open: clr
  Register #(.width(4)) register_14 (.D(EBUF_Rx), .en(1'b1), .Q(MBUF_Rx), .clk(clk));  // open: clr
  Register #(.width(1)) register_15 (.D(EBUF_WB), .en(1'b1), .Q(MBUF_WB), .clk(clk));  // open: clr

  // Other names for the same wires on the sheet: FBUF_IR[19:0] = FBUF_IMM; FBUF_Rz[3:0] = FBUF_IMM[3:0];
  //   FBUF_Ry[3:0] = FBUF_IR[23:20]; FBUF_Rx[3:0] = FBUF_IR[27:24]; FBUF_Opcode[3:0] = FBUF_IR[31:28];
  //   ID_A[31:0] = EX_RESULT; MEM_RESULT[31:0] = EX_RESULT

  // Notes on the sheet:
  //   FETCH
  //   DECODE
  //   EXECUTE
  //   MEMORY
  //   FORWARDING UNIT
endmodule

module Dual_Ported_Register_File (
  input  CLK,
  input  WrEN,
  input  [3:0] WrREGNO,
  input  [3:0] RdREGNO1,
  input  [3:0] RdREGNO2,
  input  [31:0] INPUT,
  output [31:0] OUT1,
  output [31:0] OUT2
);

  wire En_a0, En_a1, En_a2, En_at, En_fp, En_k0, En_ra, En_s0, En_s1, En_s2, En_sp, En_t0, En_t1, En_t2,
       En_v0;
  wire [31:0] a0, a1, a2, at, fp, k0, ra, s0, s1, s2, sp, t0, t1, t2, v0, zero;

  Decoder #(.select(4), .disabled(0)) decoder_1 (
    .out1(En_at), .out2(En_v0), .out3(En_a0), .out4(En_a1), .out5(En_a2), .out6(En_t0), .out7(En_t1),
    .out8(En_t2), .out9(En_s0), .out10(En_s1), .out11(En_s2), .out12(En_k0), .out13(En_sp), .out14(En_fp),
    .out15(En_ra), .sel(WrREGNO), .en(WrEN));  // open: out0
  Register #(.width(32)) u_zero (.D(INPUT), .en(1'b0), .Q(zero), .clk(CLK));  // open: clr
  Register #(.width(32)) u_at (.D(INPUT), .en(En_at), .Q(at), .clk(CLK));  // open: clr
  Register #(.width(32)) u_v0 (.D(INPUT), .en(En_v0), .Q(v0), .clk(CLK));  // open: clr
  Register #(.width(32)) u_a0 (.D(INPUT), .en(En_a0), .Q(a0), .clk(CLK));  // open: clr
  Register #(.width(32)) u_a1 (.D(INPUT), .en(En_a1), .Q(a1), .clk(CLK));  // open: clr
  Register #(.width(32)) u_a2 (.D(INPUT), .en(En_a2), .Q(a2), .clk(CLK));  // open: clr
  Register #(.width(32)) u_t0 (.D(INPUT), .en(En_t0), .Q(t0), .clk(CLK));  // open: clr
  Register #(.width(32)) u_t1 (.D(INPUT), .en(En_t1), .Q(t1), .clk(CLK));  // open: clr
  Multiplexer #(.select(4), .width(32), .disabled(0), .enable("false")) multiplexer_1 (
    .in0(zero), .in1(at), .in2(v0), .in3(a0), .in4(a1), .in5(a2), .in6(t0), .in7(t1), .in8(t2), .in9(s0),
    .in10(s1), .in11(s2), .in12(k0), .in13(sp), .in14(fp), .in15(ra), .out(OUT2), .sel(RdREGNO2));
  Register #(.width(32)) u_t2 (.D(INPUT), .en(En_t2), .Q(t2), .clk(CLK));  // open: clr
  Register #(.width(32)) u_s0 (.D(INPUT), .en(En_s0), .Q(s0), .clk(CLK));  // open: clr
  Register #(.width(32)) u_s1 (.D(INPUT), .en(En_s1), .Q(s1), .clk(CLK));  // open: clr
  Register #(.width(32)) u_s2 (.D(INPUT), .en(En_s2), .Q(s2), .clk(CLK));  // open: clr
  Register #(.width(32)) u_k0 (.D(INPUT), .en(En_k0), .Q(k0), .clk(CLK));  // open: clr
  Register #(.width(32)) u_sp (.D(INPUT), .en(En_sp), .Q(sp), .clk(CLK));  // open: clr
  Register #(.width(32)) u_fp (.D(INPUT), .en(En_fp), .Q(fp), .clk(CLK));  // open: clr
  Register #(.width(32)) u_ra (.D(INPUT), .en(En_ra), .Q(ra), .clk(CLK));  // open: clr
  Multiplexer #(.select(4), .width(32), .disabled(0), .enable("false")) multiplexer_2 (
    .in0(zero), .in1(at), .in2(v0), .in3(a0), .in4(a1), .in5(a2), .in6(t0), .in7(t1), .in8(t2), .in9(s0),
    .in10(s1), .in11(s2), .in12(k0), .in13(sp), .in14(fp), .in15(ra), .out(OUT1), .sel(RdREGNO1));

  // Notes on the sheet:
  //   MODIFY AT YOUR OWN RISK
endmodule

// FBUF
module IF_IDRR_Buffer (
  input  clk,
  output [31:0] PC,
  output [31:0] FBUF_PC,
  output [31:0] IR,
  output [31:0] FBUF_IR
);

  Register #(.width(32)) register_1 (.D(PC), .Q(FBUF_PC), .clk(clk));  // open: en, clr
  Register #(.width(32)) register_2 (.D(IR), .Q(FBUF_IR), .clk(clk));  // open: en, clr
endmodule

module ALU (
  input  [31:0] A,
  input  [31:0] B,
  input  [1:0] func,
  output [31:0] ALUout
);

  wire [31:0] adder_1_out, adder_2_out, multiplexer_1_out, nand_1_out, shifter_1_out, shifter_2_out,
       shifter_3_out;

  assign nand_1_out = ~(A & B);  // NAND_Gate nand_1, 32 bits wide
  Adder #(.width(32)) adder_1 (.a(A), .b(B), .out(adder_1_out));  // open: cin, cout
  Adder #(.width(32)) adder_2 (.a(A), .b(32'h1), .out(adder_2_out));  // open: cin, cout
  Shifter #(.width(32)) shifter_1 (.in(A), .\dist (B[4:0]), .out(shifter_1_out));
  Shifter #(.width(32), .shift("lr")) shifter_2 (.in(A), .\dist (B[4:0]), .out(shifter_2_out));
  Shifter #(.width(32), .shift("ar")) shifter_3 (.in(A), .\dist (B[4:0]), .out(shifter_3_out));
  Multiplexer #(.select(2), .width(32)) multiplexer_1 (
    .in0(shifter_1_out), .in1(shifter_2_out), .in2(shifter_1_out), .in3(shifter_3_out),
    .out(multiplexer_1_out), .sel(B[19:18]));  // open: en
  Multiplexer #(.select(2), .width(32)) multiplexer_2 (
    .in0(adder_1_out), .in1(nand_1_out), .in2(adder_2_out), .in3(multiplexer_1_out), .out(ALUout), .sel(func));  // open: en

  // Other names for the same wires on the sheet: regA[31:0] = A; dist5[4:0] = B[4:0]; regB[31:0] = B;
  //   AD[1:0] = B[19:18]
endmodule
